# Fritzing sketch sparkcopter (saved by Fritzing 0.9.1b)
circuit board: 3.85cm x 5.7cm
breadboards: 1

parts:
  GY-521 = MPU-6050 Board GY-521 [form="♀ (female)" package=THT]
  Spark_Core = Spark Core (v1.0)
  M1 = DC Motor
  M2 = DC Motor
  M3 = DC Motor
  M4 = DC Motor
  D1 = Rectifier Diode [part_number=1N4001 package="300 mil [THT]"]
  Q1 = TRANSISTOR_NPN [package=to-92-ammo]
  Q2 = TRANSISTOR_NPN [package=to-92-ammo]
  Q3 = TRANSISTOR_NPN [package=to-92-ammo]
  Q4 = TRANSISTOR_NPN [package=to-92-ammo]
  D2 = Rectifier Diode [part_number=1N4001 package="300 mil [THT]"]
  D4 = Rectifier Diode [part_number=1N4001 package="300 mil [THT]"]
  D3 = Rectifier Diode [part_number=1N4001 package="300 mil [THT]"]
  -_+ = Battery

nets:
  N1: GY-521.pin1, Spark_Core.3V3
  GND: GY-521.pin2, Spark_Core.GND, D1.anode, Q1.E, Q2.E, Q3.E, Q4.E, D2.anode, D4.anode, D3.anode, -_+.-
  N2: GY-521.pin3, Spark_Core.D1
  N3: GY-521.pin4, Spark_Core.D0
  N4: GY-521.pin8, Spark_Core.D2
  N5: Spark_Core.A0, Q1.B
  N6: Spark_Core.A1, Q2.B
  N7: Spark_Core.A4, Q4.B
  N8: Spark_Core.A5, Q3.B
  N9: Spark_Core.VIN, M1.pin_1, M2.pin_1, M3.pin_1, M4.pin_1, -_+.+
  N10: M1.pin_2, D1.cathode, Q1.C
  N11: M2.pin_2, Q2.C, D2.cathode
  N12: M3.pin_2, Q3.C, D3.cathode
  N13: M4.pin_2, Q4.C, D4.cathode

custom parts:
  MPU-6050 Board GY-521: Acelerometro y Giroscopio MPU-6050 Board GY-521
